// Logisim project full_adder.circ as structural Verilog: 1 circuit
module full_adder (
  input  A,
  input  B,
  input  Cin,
  output Sum,
  output Cout
);

  wire and_2_out, or_1_p4, or_1_p5, undriven, xor_1_p4;

  // XOR_Gate xor_1: pin names not known; wires that end beside it: A, B, B, xor_1_p4
  buf and_1 (A, undriven);  // AND_Gate
  // AND_Gate and_2 has open pins: out=and_2_out
  buf and_3 (B, undriven);  // AND_Gate
  // XOR_Gate xor_2 has open pins: out=and_2_out
  // OR_Gate or_1: pin names not known; wires that end beside it: Cin, Sum, xor_1_p4, or_1_p4, or_1_p5, Cout
endmodule
