// Logisim project sequential.circ as structural Verilog: 3 circuits
module sr_latch (
  input  S,
  input  R,
  input  CLK,
  output Q,
  output Q_N
);

  // SR_Flip_Flop #(.width(1)) sr_ff_1: pin names not known; wires that end beside it: S, R, CLK, Q, Q_N
endmodule

module d_register (
  input  [7:0] D,
  input  CLK,
  input  EN,
  input  RESET,
  output [7:0] Q
);

  // Register #(.width(8)) register_1: pin names not known; wires that end beside it: D, CLK, EN, RESET, Q
endmodule

module counter_4bit (
  input  CLK,
  input  EN,
  input  RESET,
  output [3:0] COUNT,
  output TERMINAL
);

  // Counter #(.width(4)) counter_1: pin names not known; wires that end beside it: CLK, EN, RESET, COUNT, TERMINAL
endmodule
